// Digital circuit Circuito_final.dig as structural Verilog
module Circuito_final (
  input  S1,
  input  S2,
  input  E1,
  input  E2,
  input  E3,
  input  E4,
  input  clk,
  input  L1,
  input  L2,
  input  P1,
  input  P2,
  input  P3,
  input  P4,
  output M1,
  output M2,
  output LUZ,
  output A,
  output B,
  output C,
  output D,
  output E,
  output F,
  output G,
  output DP,
  output T1,
  output T2,
  output T3,
  output T4,
  output H0
);

  wire and_1_out, and_2_out, and_3_out, and_4_out, and_5_out, and_6_out, and_7_out, and_8_out, and_9_out,
       and_10_out, and_11_out, and_12_out, and_13_out, and_14_out, and_15_out, and_16_out, and_17_out,
       and_18_out, and_19_out, and_20_out, and_21_out, and_22_out, and_23_out, and_24_out, and_25_out,
       and_26_out, and_27_out, and_29_out, and_30_out, and_31_out, and_32_out, and_33_out, and_34_out,
       and_35_out, and_36_out, and_37_out, and_38_out, and_39_out, and_40_out, and_41_out, and_42_out,
       and_43_out, and_44_out, and_45_out, and_46_out, and_47_out, and_48_out, jk_ff_1_nq, jk_ff_2_nq,
       jk_ff_3_nq, not_1_out, not_2_out, not_3_out, not_4_out, not_5_out, not_6_out, not_7_out, not_8_out,
       not_9_out, or_2_out, or_3_out, or_4_out, or_7_out, or_8_out, or_9_out, Q_0_n, Q_1_n, Q_2_n,
       xnor_1_out, xnor_2_out, xnor_3_out, xnor_4_out;

  not not_1 (not_1_out, S1);
  not not_2 (not_2_out, S2);
  not not_3 (not_3_out, Q_2_n);
  not not_4 (not_4_out, Q_1_n);
  not not_5 (not_5_out, Q_0_n);
  and and_1 (and_1_out, Q_0_n, Q_1_n, not_1_out, S2);
  and and_2 (and_2_out, Q_0_n, Q_1_n, S1, not_2_out);
  and and_3 (and_3_out, Q_0_n, Q_2_n);
  and and_4 (and_4_out, Q_1_n, Q_2_n);
  and and_5 (and_5_out, Q_2_n, not_2_out);
  and and_6 (and_6_out, Q_2_n, S1);
  and and_7 (and_7_out, not_5_out, not_4_out, Q_2_n, not_1_out, S2);
  and and_8 (and_8_out, Q_0_n, not_4_out, S1, not_2_out);
  and and_9 (and_9_out, not_5_out, Q_1_n, S1);
  and and_10 (and_10_out, not_4_out, not_3_out, S1);
  and and_11 (and_11_out, Q_1_n, not_1_out, not_2_out);
  and and_12 (and_12_out, Q_1_n, S1, S2);
  and and_13 (and_13_out, Q_0_n, not_4_out, not_3_out, not_1_out);
  and and_14 (and_14_out, Q_0_n, not_4_out, not_1_out, not_2_out);
  and and_15 (and_15_out, not_5_out, Q_1_n, not_1_out, S2);
  and and_16 (and_16_out, not_5_out, Q_1_n, S1, not_2_out);
  and and_17 (and_17_out, Q_0_n, Q_1_n, S1, S2);
  and and_18 (and_18_out, not_5_out, Q_2_n, not_1_out, S2);
  and and_19 (and_19_out, not_5_out, Q_2_n, S1, not_2_out);
  and and_20 (and_20_out, Q_0_n, Q_2_n, S1, S2);
  or or_1 (M1, Q_0_n, Q_1_n, Q_2_n, S1);
  and and_21 (and_21_out, Q_0_n, Q_1_n);
  and and_22 (and_22_out, not_5_out, not_2_out);
  and and_23 (and_23_out, Q_1_n, Q_2_n, not_2_out);
  and and_24 (and_24_out, Q_1_n, Q_2_n, S1);
  or or_2 (or_2_out, and_1_out, and_2_out, and_3_out, and_4_out, and_5_out, and_6_out);
  or or_3 (or_3_out, and_7_out, and_8_out, and_9_out, and_10_out, and_11_out, and_12_out);
  or or_4 (or_4_out, and_13_out, and_14_out, and_15_out, and_16_out, and_17_out, and_18_out, and_19_out, and_20_out);
  or or_5 (M2, and_21_out, and_22_out, Q_2_n, S1);
  or or_6 (LUZ, and_23_out, and_24_out);
  D_FF u_Q_2_n (.D(or_2_out), .C(clk), .Q(Q_2_n));  // open: nQ
  D_FF u_Q_1_n (.D(or_3_out), .C(clk), .Q(Q_1_n));  // open: nQ
  D_FF u_Q_0_n (.D(or_4_out), .C(clk), .Q(Q_0_n));  // open: nQ
  not not_6 (not_6_out, S1);
  JK_FF jk_ff_1 (.J(L1), .C(clk), .K(L1), .Q(P1), .nQ(jk_ff_1_nq));
  and and_25 (and_25_out, P1, S1);
  and and_26 (and_26_out, jk_ff_1_nq, not_6_out);
  or or_7 (or_7_out, and_25_out, and_26_out);
  JK_FF jk_ff_2 (.J(L1), .C(or_7_out), .K(L1), .Q(P2), .nQ(jk_ff_2_nq));
  xnor xnor_1 (xnor_1_out, P1, 1'b1);
  xnor xnor_2 (xnor_2_out, P2, 1'b0);
  xnor xnor_3 (xnor_3_out, P3, 1'b1);
  xnor xnor_4 (xnor_4_out, P4, 1'b0);
  and and_27 (and_27_out, jk_ff_2_nq, not_6_out);
  and and_28 (H0, xnor_1_out, xnor_2_out, xnor_3_out, xnor_4_out);
  and and_29 (and_29_out, P2, S1);
  or or_8 (or_8_out, and_29_out, and_27_out);
  JK_FF jk_ff_3 (.J(L1), .C(or_8_out), .K(L1), .Q(P3), .nQ(jk_ff_3_nq));
  and and_30 (and_30_out, P3, S1);
  and and_31 (and_31_out, jk_ff_3_nq, not_6_out);
  or or_9 (or_9_out, and_30_out, and_31_out);
  JK_FF jk_ff_4 (.J(L1), .C(or_9_out), .K(L1), .Q(P4));  // open: nQ
  not not_7 (not_7_out, P3);
  not not_8 (not_8_out, P2);
  not not_9 (not_9_out, P1);
  and and_32 (and_32_out, not_7_out, not_9_out);
  and and_33 (and_33_out, P3, P1);
  and and_34 (and_34_out, P2, P1);
  and and_35 (and_35_out, not_8_out, not_9_out);
  and and_36 (and_36_out, P2, P1);
  or or_10 (C, P3, not_8_out, P1);
  and and_37 (and_37_out, not_7_out, not_9_out);
  and and_38 (and_38_out, not_7_out, P2);
  and and_39 (and_39_out, P3, not_8_out, P1);
  and and_40 (and_40_out, P2, not_9_out);
  and and_41 (and_41_out, not_7_out, not_9_out);
  and and_42 (and_42_out, P2, not_9_out);
  and and_43 (and_43_out, P3, not_8_out);
  and and_44 (and_44_out, P3, not_9_out);
  and and_45 (and_45_out, not_8_out, not_9_out);
  and and_46 (and_46_out, not_7_out, P2);
  and and_47 (and_47_out, P3, not_8_out);
  and and_48 (and_48_out, P2, not_9_out);
  or or_11 (A, P4, and_32_out, and_33_out, and_34_out);
  or or_12 (B, not_7_out, and_35_out, and_36_out);
  or or_13 (D, and_37_out, and_38_out, and_39_out, and_40_out);
  or or_14 (E, and_41_out, and_42_out);
  or or_15 (F, P4, and_43_out, and_44_out, and_45_out);
  or or_16 (G, P4, and_46_out, and_47_out, and_48_out);
  Seven_Seg seven_seg_1 (.a(D), .b(C), .c(B), .d(A), .e(E), .f(F), .g(G), .dp(1'b0));

  assign DP = 1'b0;
  assign T1 = P1;
  assign T2 = P2;
  assign T3 = P3;
  assign T4 = P4;
endmodule
