// Digital circuit trabalho de sistemas.dig as structural Verilog
module trabalho_de_sistemas (
  input  clk,
  input  in_2,
  input  in_3,
  output out_4,
  output out_5,
  output out_6,
  output out_7
);

  wire and_1_out, and_2_out, and_3_out, and_4_out, jk_ff_1_nq, jk_ff_2_nq, not_1_out, or_1_out, or_2_out;

  not not_1 (not_1_out, in_3);
  JK_FF jk_ff_1 (.J(in_2), .C(clk), .K(in_2), .Q(out_4), .nQ(jk_ff_1_nq));
  and and_1 (and_1_out, out_4, in_3);
  and and_2 (and_2_out, jk_ff_1_nq, not_1_out);
  or or_1 (or_1_out, and_1_out, and_2_out);
  JK_FF jk_ff_2 (.J(in_2), .C(or_1_out), .K(in_2), .Q(out_5), .nQ(jk_ff_2_nq));
  and and_3 (and_3_out, jk_ff_2_nq, not_1_out);
  and and_4 (and_4_out, out_5, in_3);
  or or_2 (or_2_out, and_4_out, and_3_out);
  JK_FF jk_ff_3 (.C(or_2_out));  // open: J, K, Q, nQ
  JK_FF jk_ff_4 ();  // open: J, C, K, Q, nQ
endmodule
